# Fritzing sketch PCB_compactadora (saved by Fritzing 0.9.9b)
circuit board: 15cm x 10cm
breadboards: 1

parts:
  Arduino_MEGA = Arduino Mega 2560 (Rev3)
  ON/OFF_Switch = SIP - 2 pins [chip_label=cambiar package="SIP (Single Inline) [THT]"]
  Switch_magnetico = SIP - 2 pins [chip_label=cambiar package="SIP (Single Inline) [THT]"]
  Speaker = SIP - 2 pins [chip_label=cambiar package="SIP (Single Inline) [THT]"]
  Red_LED = SIP - 2 pins [chip_label=cambiar package="SIP (Single Inline) [THT]"]
  Green_LED = SIP - 2 pins [chip_label=cambiar package="SIP (Single Inline) [THT]"]
  Compact_button = SIP - 2 pins [chip_label=cambiar package="SIP (Single Inline) [THT]"]
  Lift_Button = SIP - 2 pins [chip_label=cambiar package="SIP (Single Inline) [THT]"]
  Emergency_button = SIP - 2 pins [chip_label=cambiar package="SIP (Single Inline) [THT]"]
  Pantalla_tactil = IC, SIP package, 4 pins [chip_label=NX8048K070]
  V1A = DC Power [voltage=5V]
  Load_Cell3 = Load Cell - Red/white/black/green
  Part5 = HX711 Weighing Sensor Module
  Relevador0 = IC, DIP package, 6 pins
  Relevador1 = IC, DIP package, 6 pins
  Relevador2 = IC, DIP package, 6 pins
  Relevador3 = IC, DIP package, 6 pins  # not connected
  Relevador4 = IC, DIP package, 6 pins  # not connected
  V1A1 = DC Power [voltage=5V]  # not connected

nets (from the schematic view):
  GND: Arduino_MEGA.GND, ON/OFF_Switch.pin2, Switch_magnetico.pin2, Speaker.pin2, Red_LED.pin2, Green_LED.pin2, Compact_button.pin2, Lift_Button.pin2, Emergency_button.pin2, Pantalla_tactil.pin1, V1A.V-, Part5.GND, Relevador0.pin2
  N1: Arduino_MEGA.D9_PWM, Speaker.pin1
  5V: Arduino_MEGA.5V, Part5.VCC, Relevador0.pin1, Relevador1.pin1, Relevador2.pin1
  N2: Arduino_MEGA.D0_RX0, Pantalla_tactil.pin3
  N3: Arduino_MEGA.D1_TX0, Pantalla_tactil.pin2
  N4: Arduino_MEGA.D3_PWM, ON/OFF_Switch.pin1
  N5: Arduino_MEGA.D4_PWM, Part5.DO/RX
  N6: Arduino_MEGA.D5_PWM, Part5.CK/TX
  N7: Arduino_MEGA.D23, Switch_magnetico.pin1
  N8: Arduino_MEGA.D26, Relevador0.pin3
  N9: Arduino_MEGA.D33, Lift_Button.pin1
  N10: Arduino_MEGA.D35, Emergency_button.pin1
  N11: Arduino_MEGA.D37, Compact_button.pin1
  N12: Arduino_MEGA.D42, Green_LED.pin1
  N13: Arduino_MEGA.D46, Red_LED.pin1
  N14: Pantalla_tactil.pin4, Relevador0.pin4
  N15: V1A.V+, Relevador0.pin5
  N16: Load_Cell3.wire1, Part5.E+
  N17: Load_Cell3.wire2, Part5.A+
  N18: Load_Cell3.wire3, Part5.E-
  N19: Load_Cell3.wire4, Part5.A-

custom parts:
  Load Cell - Red/white/black/green: A rectangle load cell/weighting pressure Sensor with four wires - Red, white, black, green. Normally corresponding with E+, E-, A+, A- respectively.
  HX711 Weighing Sensor Module: HX711 is a precision 24-bit analog-to-digital converter (ADC) designed for weigh scales and industrial control applications to interface directly with a bridge sensor.
